// Logisim project lab8.circ as structural Verilog: 1 circuit, main circuit main
module main (
  input  RegWrite,
  input  [1:0] ReadReg1,
  input  [7:0] RegDataW,
  input  [1:0] WriteReg,
  input  [1:0] ReadReg2,
  output [7:0] RegData1,
  output [7:0] RegData2
);

  wire and_1_out, and_2_out, and_3_out, and_4_out, decoder_1_out0, decoder_1_out1, decoder_1_out2,
       decoder_1_out3, theClock_out;
  wire [7:0] X0_q, X1_q, X2_q, X3_q;

  Decoder #(.enable("false"), .select(2)) decoder_1 (
    .out0(decoder_1_out0), .out1(decoder_1_out1), .out2(decoder_1_out2), .out3(decoder_1_out3), .sel(WriteReg));
  Clock theClock (.out(theClock_out));
  and and_1 (and_1_out, RegWrite, decoder_1_out0);
  and and_2 (and_2_out, RegWrite, decoder_1_out1);
  and and_3 (and_3_out, decoder_1_out2, RegWrite);
  and and_4 (and_4_out, decoder_1_out3, RegWrite);
  Register X0 (.D(RegDataW), .en(and_1_out), .clk(theClock_out), .Q(X0_q));  // open: clr
  Register X1 (.D(RegDataW), .en(and_2_out), .clk(theClock_out), .Q(X1_q));  // open: clr
  Register X2 (.D(RegDataW), .en(and_3_out), .clk(theClock_out), .Q(X2_q));  // open: clr
  Register X3 (.D(RegDataW), .en(and_4_out), .clk(theClock_out), .Q(X3_q));  // open: clr
  Multiplexer #(.select(2), .width(8)) multiplexer_1 (
    .in0(X0_q), .in1(X1_q), .in2(X2_q), .in3(X3_q), .out(RegData1), .sel(ReadReg1));
  Multiplexer #(.select(2), .width(8)) multiplexer_2 (
    .in0(X0_q), .in1(X1_q), .in2(X2_q), .in3(X3_q), .out(RegData2), .sel(ReadReg2));

  // Notes on the sheet:
  //   Daniel Detore, Elliott McKelvey
  //   I pledge my honor that I have abided by the Stevens Honor System.
endmodule
