// Logisim project basics.circ as structural Verilog: 2 circuits, main circuit main
module main (
  output [15:0] instruction
);

  wire and_1_out, and_2_out, and_3_out, and_4_out, and_5_out, clock_1_out, clock_2_out, clock_3_out,
       decoder_1_out0, decoder_1_out1, decoder_1_out2, decoder_1_out3, not_1_out, not_2_out;
  wire [7:0] adder_1_out, adder_2_out, DataMemory_dout, divider_1_out, multiplexer_1_out, multiplexer_2_out,
       multiplexer_3_out, multiplexer_4_out, multiplexer_5_out, multiplexer_6_out, PC_q, R0_q, R1_q, R2_q,
       R3_q;

  Register PC (.D(adder_1_out), .en(1'b1), .clk(clock_1_out), .Q(PC_q));  // open: clr
  Clock clock_1 (.out(clock_1_out));
  Decoder #(.enable("false"), .select(2)) decoder_1 (
    .out0(decoder_1_out0), .out1(decoder_1_out1), .out2(decoder_1_out2), .out3(decoder_1_out3),
    .sel(instruction[11:10]));
  Adder adder_1 (.a(8'h1), .b(PC_q), .out(adder_1_out));  // open: cin, cout
  RAM #(.dataWidth(16), .enables("line")) instructionMemory (
    .addr(PC_q), .we(1'b0), .clk(clock_1_out), .dout(instruction));  // open: din
  not not_1 (not_1_out, instruction[14]);
  Clock clock_2 (.out(clock_2_out));
  and and_1 (and_1_out, not_1_out, decoder_1_out0);
  and and_2 (and_2_out, not_1_out, decoder_1_out1);
  and and_3 (and_3_out, decoder_1_out2, not_1_out);
  and and_4 (and_4_out, decoder_1_out3, not_1_out);
  Register R0 (.D(multiplexer_1_out), .en(and_1_out), .clk(clock_2_out), .Q(R0_q));  // open: clr
  Register R1 (.D(multiplexer_1_out), .en(and_2_out), .clk(clock_2_out), .Q(R1_q));  // open: clr
  Register R2 (.D(multiplexer_1_out), .en(and_3_out), .clk(clock_2_out), .Q(R2_q));  // open: clr
  Register R3 (.D(multiplexer_1_out), .en(and_4_out), .clk(clock_2_out), .Q(R3_q));  // open: clr
  Multiplexer #(.width(8)) multiplexer_1 (
    .in0(multiplexer_6_out), .in1(DataMemory_dout), .out(multiplexer_1_out), .sel(instruction[15]));
  not not_2 (not_2_out, instruction[12]);
  Multiplexer #(.select(2), .width(8)) multiplexer_2 (
    .in0(R0_q), .in1(R1_q), .in2(R2_q), .in3(R3_q), .out(multiplexer_2_out), .sel(instruction[9:8]));
  and and_5 (and_5_out, instruction[14], not_2_out);
  Multiplexer #(.select(2), .width(8)) multiplexer_3 (
    .in0(R0_q), .in1(R1_q), .in2(R2_q), .in3(R3_q), .out(multiplexer_3_out), .sel(instruction[7:6]));
  Multiplexer #(.width(8)) multiplexer_4 (
    .in0(multiplexer_3_out), .in1(multiplexer_2_out), .out(multiplexer_4_out), .sel(and_5_out));
  Multiplexer #(.width(8)) multiplexer_5 (
    .in0(multiplexer_3_out), .in1(instruction[7:0]), .out(multiplexer_5_out), .sel(instruction[12]));
  RAM #(.enables("line")) DataMemory (
    .addr(multiplexer_6_out), .we(instruction[14]), .clk(clock_3_out), .din(multiplexer_4_out),
    .dout(DataMemory_dout));
  Clock clock_3 (.out(clock_3_out));
  Adder adder_2 (.a(multiplexer_2_out), .b(multiplexer_5_out), .out(adder_2_out));  // open: cin, cout
  Divider divider_1 (.a(multiplexer_2_out), .b(multiplexer_5_out), .out(divider_1_out));  // open: upper, rem
  Multiplexer #(.width(8)) multiplexer_6 (
    .in0(adder_2_out), .in1(divider_1_out), .out(multiplexer_6_out), .sel(instruction[13]));

  // Notes on the sheet:
  //   WriteReg
  //   RegWrite
  //   MemWrite
  //   RegDataW
  //   ReadToReg
  //   ALUout
  //   ReadDataM
  //   MemWrite
  //   UseImm
  //   ReadReg1
  //   RegData1
  //   ReadReg2
  //   RegData2
  //   RegData2
  //   imm
  //   WriteDataM
  //   UseImm
  //   ALUout
  //   ALUop
endmodule

module CustomDivider (
  input  [7:0] Numerator,
  input  [7:0] Denominator
);
endmodule
