// Logisim project sqrtr.circ as structural Verilog: 2 circuits, main circuit main
module main (
);

  wire and_1_out, and_2_out, and_3_out, and_4_out, clock_1_out, clock_2_out, clock_3_out, decoder_1_out0,
       decoder_1_out1, decoder_1_out2, decoder_1_out3, not_1_out;
  wire [7:0] adder_1_out, adder_2_out, dataMemory_dout, Divider_quotient, multiplexer_1_out,
       multiplexer_2_out, multiplexer_3_out, multiplexer_4_out, multiplexer_5_out, multiplexer_6_out, PC_q,
       R0_q, R1_q, R2_q, R3_q;
  wire [15:0] instructionMemory_dout;

  Register PC (.D(adder_1_out), .en(1'b1), .clk(clock_1_out), .Q(PC_q));  // open: clr
  Clock clock_1 (.out(clock_1_out));
  Decoder #(.enable("false"), .select(2)) decoder_1 (
    .out0(decoder_1_out0), .out1(decoder_1_out1), .out2(decoder_1_out2), .out3(decoder_1_out3),
    .sel(instructionMemory_dout[11:10]));
  Adder adder_1 (.a(8'h1), .b(PC_q), .out(adder_1_out));  // open: cin, cout
  RAM #(.dataWidth(16), .enables("line")) instructionMemory (
    .addr(PC_q), .we(1'b0), .clk(clock_1_out), .dout(instructionMemory_dout));  // open: din
  not not_1 (not_1_out, instructionMemory_dout[14]);
  Clock clock_2 (.out(clock_2_out));
  and and_1 (and_1_out, not_1_out, decoder_1_out0);
  and and_2 (and_2_out, not_1_out, decoder_1_out1);
  and and_3 (and_3_out, decoder_1_out2, not_1_out);
  and and_4 (and_4_out, decoder_1_out3, not_1_out);
  Register R0 (.D(multiplexer_1_out), .en(and_1_out), .clk(clock_2_out), .Q(R0_q));  // open: clr
  Register R1 (.D(multiplexer_1_out), .en(and_2_out), .clk(clock_2_out), .Q(R1_q));  // open: clr
  Register R2 (.D(multiplexer_1_out), .en(and_3_out), .clk(clock_2_out), .Q(R2_q));  // open: clr
  Register R3 (.D(multiplexer_1_out), .en(and_4_out), .clk(clock_2_out), .Q(R3_q));  // open: clr
  Multiplexer #(.width(8)) multiplexer_1 (
    .in0(multiplexer_6_out), .in1(dataMemory_dout), .out(multiplexer_1_out), .sel(instructionMemory_dout[15]));
  Multiplexer #(.select(2), .width(8)) multiplexer_2 (
    .in0(R0_q), .in1(R1_q), .in2(R2_q), .in3(R3_q), .out(multiplexer_2_out), .sel(instructionMemory_dout[9:8]));
  Multiplexer #(.select(2), .width(8)) multiplexer_3 (
    .in0(R0_q), .in1(R1_q), .in2(R2_q), .in3(R3_q), .out(multiplexer_3_out), .sel(instructionMemory_dout[7:6]));
  Multiplexer #(.width(8)) multiplexer_4 (
    .in0(instructionMemory_dout[7:0]), .in1({2'b00, instructionMemory_dout[5:0]}), .out(multiplexer_4_out),
    .sel(instructionMemory_dout[14]));
  Multiplexer #(.width(8)) multiplexer_5 (
    .in0(multiplexer_3_out), .in1(multiplexer_4_out), .out(multiplexer_5_out),
    .sel(instructionMemory_dout[12]));
  RAM #(.enables("line")) dataMemory (
    .addr(multiplexer_6_out), .we(instructionMemory_dout[14]), .clk(clock_3_out), .din(multiplexer_3_out),
    .dout(dataMemory_dout));
  Clock clock_3 (.out(clock_3_out));
  Adder adder_2 (.a(multiplexer_2_out), .b(multiplexer_5_out), .out(adder_2_out));  // open: cin, cout
  CustomDivider Divider (
    .Numerator(multiplexer_2_out), .Denominator(multiplexer_5_out), .Quotient(Divider_quotient));  // open: Remainder
  Multiplexer #(.width(8)) multiplexer_6 (
    .in0(adder_2_out), .in1(Divider_quotient), .out(multiplexer_6_out), .sel(instructionMemory_dout[13]));

  // Notes on the sheet:
  //   WriteReg
  //   RegWrite
  //   MemWrite
  //   RegDataW
  //   MemRead
  //   ALUout
  //   ReadDataM
  //   Daniel Detore
  //   I pledge my honor that I have abided by the Stevens Honor System.
  //   ReadReg1
  //   RegData1
  //   imm8
  //   ReadReg2
  //   RegData2
  //   imm6
  //   imm
  //   WriteDataM
  //   MemWrite
  //   UseImm
  //   ALUout
  //   ALUop
endmodule

module CustomDivider (
  input  [7:0] Numerator,
  input  [7:0] Denominator,
  output [7:0] Quotient,
  output [7:0] Remainder
);

  wire comparator_1_lt, nor_1_out, nor_2_out, nor_3_out, nor_4_out, nor_5_out, nor_6_out, nor_7_out,
       nor_8_out, nor_9_out, not_1_out, not_2_out, not_3_out, not_4_out, not_5_out, not_6_out, not_7_out,
       not_8_out, or_1_out, subtractor_1_bout, subtractor_2_bout, subtractor_3_bout, subtractor_4_bout,
       subtractor_5_bout, subtractor_6_bout, subtractor_7_bout, subtractor_8_bout;
  wire [7:0] and_8_out, multiplexer_1_out, multiplexer_2_out, multiplexer_3_out, multiplexer_5_out,
       multiplexer_6_out, multiplexer_7_out, multiplexer_8_out, subtractor_1_out, subtractor_2_out,
       subtractor_3_out, subtractor_4_out, subtractor_5_out, subtractor_6_out, subtractor_7_out,
       subtractor_8_out;

  Comparator #(.mode("unsigned")) comparator_1 (.a(Numerator), .b(Denominator), .lt(comparator_1_lt));  // open: gt, eq
  Subtractor subtractor_1 (
    .a(Numerator), .b({Denominator[0], {7{1'b0}}}), .out(subtractor_1_out), .bout(subtractor_1_bout));  // open: bin
  not not_1 (not_1_out, subtractor_1_bout);
  nor nor_1 (nor_1_out, Denominator[1], Denominator[2], Denominator[3], Denominator[4], Denominator[6], Denominator[7], 1'b0, Denominator[5]);
  and and_1 (and_8_out[7], not_1_out, nor_1_out);
  Multiplexer #(.width(8)) multiplexer_1 (
    .in0(Numerator), .in1(subtractor_1_out), .out(multiplexer_1_out), .sel(and_8_out[7]));
  Subtractor subtractor_2 (
    .a(multiplexer_1_out), .b({Denominator[1:0], {6{1'b0}}}), .out(subtractor_2_out), .bout(subtractor_2_bout));  // open: bin
  nor nor_2 (nor_2_out, Denominator[2], Denominator[3], Denominator[4], Denominator[5], Denominator[7], 1'b0, 1'b0, Denominator[6]);
  not not_2 (not_2_out, subtractor_2_bout);
  and and_2 (and_8_out[6], not_2_out, nor_2_out);
  Multiplexer #(.width(8)) multiplexer_2 (
    .in0(multiplexer_1_out), .in1(subtractor_2_out), .out(multiplexer_2_out), .sel(and_8_out[6]));
  nor nor_3 (nor_3_out, Denominator[0], Denominator[1], Denominator[2], Denominator[3], Denominator[5], Denominator[6], Denominator[7], Denominator[4]);
  Subtractor subtractor_3 (
    .a(multiplexer_2_out), .b({Denominator[2:0], {5{1'b0}}}), .out(subtractor_3_out), .bout(subtractor_3_bout));  // open: bin
  not not_3 (not_3_out, subtractor_3_bout);
  nor nor_4 (nor_4_out, Denominator[3], Denominator[4], Denominator[5], Denominator[6], 1'b0, 1'b0, 1'b0, Denominator[7]);
  and and_3 (and_8_out[5], not_3_out, nor_4_out);
  or or_1 (or_1_out, nor_3_out, comparator_1_lt);
  Multiplexer #(.width(8)) multiplexer_3 (
    .in0(multiplexer_2_out), .in1(subtractor_3_out), .out(multiplexer_3_out), .sel(and_8_out[5]));
  Multiplexer #(.width(8)) multiplexer_4 (.in0(and_8_out), .in1({8{1'b0}}), .out(Quotient), .sel(or_1_out));
  Subtractor subtractor_4 (
    .a(multiplexer_3_out), .b({Denominator[3:0], 4'b0000}), .out(subtractor_4_out), .bout(subtractor_4_bout));  // open: bin
  not not_4 (not_4_out, subtractor_4_bout);
  nor nor_5 (nor_5_out, Denominator[4], Denominator[5], Denominator[6], Denominator[7], 1'b0, 1'b0, 1'b0, 1'b0);
  Multiplexer #(.width(8)) multiplexer_5 (
    .in0(multiplexer_3_out), .in1(subtractor_4_out), .out(multiplexer_5_out), .sel(and_8_out[4]));
  and and_4 (and_8_out[4], not_4_out, nor_5_out);
  Subtractor subtractor_5 (
    .a(multiplexer_5_out), .b({Denominator[4:0], 3'b000}), .out(subtractor_5_out), .bout(subtractor_5_bout));  // open: bin
  not not_5 (not_5_out, subtractor_5_bout);
  nor nor_6 (nor_6_out, Denominator[5], Denominator[6], Denominator[7], 1'b0, 1'b0, 1'b0, 1'b0, 1'b0);
  and and_5 (and_8_out[3], not_5_out, nor_6_out);
  Multiplexer #(.width(8)) multiplexer_6 (
    .in0(multiplexer_5_out), .in1(subtractor_5_out), .out(multiplexer_6_out), .sel(and_8_out[3]));
  Subtractor subtractor_6 (
    .a(multiplexer_6_out), .b({Denominator[5:0], 2'b00}), .out(subtractor_6_out), .bout(subtractor_6_bout));  // open: bin
  not not_6 (not_6_out, subtractor_6_bout);
  nor nor_7 (nor_7_out, Denominator[6], Denominator[7], 1'b0, 1'b0, 1'b0, 1'b0, 1'b0, 1'b0);
  and and_6 (and_8_out[2], not_6_out, nor_7_out);
  Multiplexer #(.width(8)) multiplexer_7 (
    .in0(multiplexer_6_out), .in1(subtractor_6_out), .out(multiplexer_7_out), .sel(and_8_out[2]));
  Subtractor subtractor_7 (
    .a(multiplexer_7_out), .b({Denominator[6:0], 1'b0}), .out(subtractor_7_out), .bout(subtractor_7_bout));  // open: bin
  not not_7 (not_7_out, subtractor_7_bout);
  nor nor_8 (nor_8_out, Denominator[7], 1'b0, 1'b0, 1'b0, 1'b0, 1'b0, 1'b0, 1'b0);
  Multiplexer #(.width(8)) multiplexer_8 (
    .in0(multiplexer_7_out), .in1(subtractor_7_out), .out(multiplexer_8_out), .sel(and_8_out[1]));
  and and_7 (and_8_out[1], not_7_out, nor_8_out);
  Subtractor subtractor_8 (
    .a(multiplexer_8_out), .b(Denominator), .out(subtractor_8_out), .bout(subtractor_8_bout));  // open: bin
  not not_8 (not_8_out, subtractor_8_bout);
  nor nor_9 (nor_9_out, 1'b0, 1'b0, 1'b0, 1'b0, 1'b0, 1'b0, 1'b0, 1'b0);
  and and_8 (and_8_out[0], not_8_out, nor_9_out);
  Multiplexer #(.width(8)) multiplexer_9 (
    .in0(multiplexer_8_out), .in1(subtractor_8_out), .out(Remainder), .sel(and_8_out[0]));
endmodule
